# Fritzing sketch Untitled Sketch (saved by Fritzing 0.9.3b)
circuit board: 7.06074cm x 6.16029cm
breadboards: 1

parts:
  NODEMCU1_0 = NodeMCU V1.0
  BLUETOOTH = Header 6 [package=molex-1x6-ra]
  DHT22 = Header 3 [package=molex-1x3_lock]
  PMS3003 = Header 4 [package=molex-1x4_lock]
  I2C-MODULE = Header 4 [package=molex-1x4_lock]
  BC547 = PNP-Transistor [package="TO92 [THT]"]
  BT-BUTTON = Camdenboss CTB0158-2 [part_number=CTB0158-2 package=THT]
  EXTERNAL_SUPPLY = Camdenboss CTB0158-2 [part_number=CTB0158-2 package=THT]  # not connected

nets:
  N1: NODEMCU1_0.D0, BLUETOOTH.2
  N2: NODEMCU1_0.D1, I2C-MODULE.1
  N3: NODEMCU1_0.D2, I2C-MODULE.2
  N4: NODEMCU1_0.D3, PMS3003.3
  N5: NODEMCU1_0.D4, BLUETOOTH.3
  N6: NODEMCU1_0.GND, DHT22.3, PMS3003.1, I2C-MODULE.4, BC547.C, BT-BUTTON.pin2
  N7: NODEMCU1_0.D5, PMS3003.4
  N8: NODEMCU1_0.D6, DHT22.2
  N9: NODEMCU1_0.D7, BT-BUTTON.pin1
  N10: NODEMCU1_0.D8, BC547.B
  N11: NODEMCU1_0.Vin, BLUETOOTH.5, DHT22.1, PMS3003.2, I2C-MODULE.3
  N12: BLUETOOTH.4, BC547.E

notes:
  GND
  VCC
  Rx
  Tx
  D
  SCL
  SDA
  STATE
  EN_M

custom parts:
  NodeMCU V1.0: ESP8266 based NodeMCU
