# Fritzing sketch circuit-diagram (saved by Fritzing 0.9.3b)

parts:
  Part1 = Arduino Uno (Rev3)
  Part2 = Arduino Uno (Rev3)

nets:
  N1: Part1.D9_PWM, Part2.D10_PWM/SS
  N2: Part1.D10_PWM/SS, Part2.D9_PWM
  GND: Part1.GND, Part2.GND
